# Fritzing sketch Fritzing_Devre (saved by Fritzing 0.9.3b)
breadboards: 2

parts:
  GY1 = GY-521 (MPU-6050) [form="♀ (female)" package=THT]
  Parça1 = Arduino Uno (Rev3)
  S2 = Pushbutton [package=THT]
  S3 = Pushbutton [package=THT]

nets:
  N1: GY1.pin1, Parça1.3V3
  N2: GY1.pin2, Parça1.GND, S2.leg0, S3.leg0
  N3: GY1.pin3, Parça1.A5/SCL
  N4: GY1.pin4, Parça1.A4/SDA
  N5: GY1.pin8, Parça1.D2
  N6: Parça1.D8, S2.leg1
  N7: Parça1.D9_PWM, S3.leg1

notes:
  MPU6050
  VCC --> 3V3
  GND --> GND
  SCL --> A5
  SDA --> A4
  INT --> PIN2
  SOL TIK - SAĞ TIK
  PIN9 - PIN8

custom parts:
  GY-521 (MPU-6050): Placa GY-521 basada en conjunto de acelerómetro+giroscopios MPU-6050
